# Fritzing sketch Module Coeur de LEDs (allongé) (saved by Fritzing 0.9.3b)
breadboards: 1

parts:
  LED1 = LED - 5mm [color="Red (633nm)" package="5 mm [THT]"]
  LED2 = LED - 5mm [color="Red (633nm)" package="5 mm [THT]"]
  LED3 = LED - 5mm [color="Red (633nm)" package="5 mm [THT]"]
  LED4 = LED - 5mm [color="Red (633nm)" package="5 mm [THT]"]
  LED5 = LED - 5mm [color="Red (633nm)" package="5 mm [THT]"]
  LED6 = LED - 5mm [color="Red (633nm)" package="5 mm [THT]"]
  LED7 = LED - 5mm [color="Red (633nm)" package="5 mm [THT]"]
  LED8 = LED - 5mm [color="Red (633nm)" package="5 mm [THT]"]
  LED9 = LED - 5mm [color="Red (633nm)" package="5 mm [THT]"]
  LED10 = LED - 5mm [color="Red (633nm)" package="5 mm [THT]"]
  R1 = Resistor [tolerance=±5% resistance=220 package=THT]
  R2 = Resistor [tolerance=±5% resistance=220 package=THT]
  R3 = Resistor [tolerance=±5% resistance=220 package=THT]
  R4 = Resistor [tolerance=±5% resistance=220 package=THT]
  R5 = Resistor [tolerance=±5% resistance=220 package=THT]
  R6 = Resistor [tolerance=±5% resistance=220 package=THT]
  R7 = Resistor [tolerance=±5% resistance=220 package=THT]
  R8 = Resistor [tolerance=±5% resistance=220 package=THT]
  R9 = Resistor [tolerance=±5% resistance=220 package=THT]
  R10 = Resistor [tolerance=±5% resistance=220 package=THT]
  Composant1 = Arduino Uno (Rev3)

nets:
  N1: LED1.cathode, Composant1.D6_PWM
  N2: LED1.anode, R2.Pin_0
  N3: LED2.cathode, LED2.anode, R9.Pin_0, Composant1.D9_PWM
  N4: LED3.cathode, LED3.anode, R3.Pin_0, Composant1.D8
  N5: LED4.cathode, LED4.anode, R4.Pin_0, Composant1.D10_PWM/SS
  N6: LED5.cathode, LED5.anode, R5.Pin_0, Composant1.D12/MISO
  N7: LED6.cathode, LED6.anode, R7.Pin_0, Composant1.D4
  N8: LED7.cathode, LED7.anode, R10.Pin_0, Composant1.D11_PWM/MOSI
  N9: LED8.cathode, LED8.anode, R8.Pin_0, Composant1.D7
  N10: LED9.cathode, Composant1.D13/SCK
  N11: LED9.anode, R6.Pin_0
  N12: LED10.cathode, LED10.anode, R1.Pin_0, Composant1.D5_PWM
  N13: R1.Pin_1, R2.Pin_1, R3.Pin_1, R4.Pin_1, R5.Pin_1, R6.Pin_1, R7.Pin_1, R8.Pin_1, R9.Pin_1, R10.Pin_1, Composant1.GND
